// Logisim project ControlUnit.circ as structural Verilog: 1 circuit, main circuit Control Unit
module Control_Unit (
  input  [19:0] in_1,
  input  [19:0] in_2,
  input  in_3,
  input  [2:0] in_4,
  output out_5,
  output [19:0] out_6,
  output out_7
);

  Clock clock_1 ();  // open: out
  ALU alu_1 (.N0(in_1), .N1(in_2), .S3(in_4), .ES(in_3), .O(out_5), .R(out_6), .E(out_7));
  // Memory memory_1: pin names not known
endmodule
